// Logisim project main.circ as structural Verilog
module main (
  output out_1
);

  wire and_1_out, and_2_out, and_3_out, and_4_out, and_5_out, changePCx, changePCy, chGM, comparator_2_eq,
       comparator_3_eq, comparator_4_eq, comparator_5_eq, comparator_6_eq, comparator_7_eq, comparator_8_eq,
       comparator_9_eq, comparator_10_eq, comparator_11_eq, gS0, gS1, gS2, InpFl, InpFlmove1, InpFlmove2,
       InpFlpre, letsPrint, LoadMap, mainClk, mainRES, MapLevelCh, memReadyToPrint, not_1_out, not_2_out,
       not_3_out, not_4_out, not_5_out, not_6_out, not_7_out, not_8_out, not_9_out, not_10_out, not_11_out,
       not_12_out, not_13_out, not_14_out, not_15_out, not_16_out, not_17_out, not_18_out, or_2_out,
       or_3_out, or_4_out, or_7_out, or_9_out, PlDirCh, register_9_q, register_10_q, StateCh, TOPRINTCh,
       TOPRINTRES, WonInp;
  wire [1:0] adder_1_out, NewPlDir, PlDir, subtractor_1_out;
  wire [3:0] gameState, gSto;
  wire [7:0] adder_2_out, adder_3_out, adder_4_out, adder_5_out, gStdtScrMem, InpKey, mapLevelCur,
       maps_1_xpp, maps_1_ypp, memChar, multiplexer_1_out, multiplexer_2_out, NewMapLevelCh, NewPLxOM,
       NewPLyOM, NewTextTOPRINT, p_x_1_y, p_x_1_y_t, p_x_y, p_x_y_1, p_x_y_1_t, PLxOM, PLyOM,
       subtractor_2_out, subtractor_3_out, subtractor_4_out, subtractor_5_out, textTOPRINT;
  wire [11:0] MapH, maps_1_height, maps_1_width, MapW, memN, tpLen, x_y_____elem_2_elem, x_y_____elem_3_elem,
       x_y_____elem_4_elem, x_y_____elem_5_elem, x_y_____elem_elem;

  or or_1 (letsPrint, memReadyToPrint, gS0);
  Multiplexer #(.width(8)) multiplexer_1 (
    .in0(NewPLxOM), .in1(maps_1_xpp), .out(multiplexer_1_out), .sel(gS0));  // open: en
  or or_2 (or_2_out, changePCx, LoadMap);
  Register #(.width(12)) u_mapW (.D(maps_1_width), .Q(MapW), .clk(LoadMap));  // open: en, clr
  not not_1 (not_1_out, InpFlpre);
  Clock clock_1 (.out(mainClk));
  Button button_1 (.out(mainRES));
  consoler CONSOLE_PRINTER (
    .CLK(mainClk), .RESET(letsPrint), .IT_WORKED(InpFlpre), .INPUT_CHAR(InpKey), .PRINT_SIZE(tpLen),
    .MEM_A(memN), .MEM_D(memChar));
  Register Xpp (.D(multiplexer_1_out), .Q(PLxOM), .clk(or_2_out));  // open: en, clr
  Register #(.width(1)) register_1 (.D(InpFlpre), .Q(TOPRINTRES), .clk(InpFlpre), .clr(not_2_out));  // open: en
  not not_2 (not_2_out, not_1_out);
  Register Ypp (.D(multiplexer_2_out), .Q(PLyOM), .clk(or_3_out));  // open: en, clr
  Multiplexer #(.width(8)) multiplexer_2 (
    .in0(NewPLyOM), .in1(maps_1_ypp), .out(multiplexer_2_out), .sel(gS0));  // open: en
  or or_3 (or_3_out, changePCy, LoadMap);
  maps maps_1 (
    .ADDR(mapLevelCur), .ELEM(12'h1), .Xpp(maps_1_xpp), .Ypp(maps_1_ypp), .Width(maps_1_width),
    .Height(maps_1_height));  // open: DATA, LEN
  Register #(.width(12)) u_mapH (.D(maps_1_height), .Q(MapH), .clk(LoadMap));  // open: en, clr
  Comparator comparator_1 (.a(InpKey), .b(8'h77), .eq(WonInp));  // open: gt, lt
  Comparator #(.width(2)) comparator_2 (.a(PlDir), .b(2'b00), .eq(comparator_2_eq));  // open: gt, lt
  Comparator #(.width(2)) comparator_3 (.a(PlDir), .b(2'b10), .eq(comparator_3_eq));  // open: gt, lt
  Comparator #(.width(2)) comparator_4 (.a(PlDir), .b(2'b01), .eq(comparator_4_eq));  // open: gt, lt
  Comparator #(.width(2)) comparator_5 (.a(PlDir), .b(2'b11), .eq(comparator_5_eq));  // open: gt, lt
  Comparator comparator_6 (.a(p_x_y_1_t), .b(8'h23), .eq(comparator_6_eq));  // open: gt, lt
  not not_3 (not_3_out, comparator_6_eq);
  Comparator comparator_7 (.a(p_x_y_1), .b(8'h23), .eq(comparator_7_eq));  // open: gt, lt
  not not_4 (not_4_out, comparator_7_eq);
  not not_5 (not_5_out, comparator_8_eq);
  Comparator comparator_8 (.a(p_x_1_y), .b(8'h23), .eq(comparator_8_eq));  // open: gt, lt
  Comparator comparator_9 (.a(p_x_1_y_t), .b(8'h23), .eq(comparator_9_eq));  // open: gt, lt
  not not_6 (not_6_out, comparator_9_eq);
  Register register_2 (.D(NewMapLevelCh), .Q(mapLevelCur), .clk(MapLevelCh), .clr(mainRES));  // open: en
  Register register_3 (.D(NewTextTOPRINT), .Q(textTOPRINT), .clk(TOPRINTCh), .clr(or_4_out));  // open: en
  or or_4 (or_4_out, mainRES, TOPRINTRES);
  Comparator comparator_10 (.a(InpKey), .b(8'h61), .eq(comparator_10_eq));  // open: gt, lt
  or or_5 (InpFlmove1, comparator_10_eq, comparator_11_eq);
  not not_7 (not_7_out, InpFlmove1);
  Comparator comparator_11 (.a(InpKey), .b(8'h64), .eq(comparator_11_eq));  // open: gt, lt
  and and_1 (and_1_out, not_3_out, WonInp, comparator_2_eq);
  and and_2 (and_2_out, not_4_out, WonInp, comparator_3_eq);
  and and_3 (and_3_out, not_5_out, WonInp, comparator_4_eq);
  and and_4 (and_4_out, not_6_out, WonInp, comparator_5_eq);
  Adder #(.width(2)) adder_1 (.a(PlDir), .b(2'b01), .out(adder_1_out));  // open: cin, cout
  Subtractor #(.width(2)) subtractor_1 (.a(PlDir), .b(2'b01), .out(subtractor_1_out));  // open: bin, bout
  not not_8 (not_8_out, not_7_out);
  Register #(.width(1)) register_4 (.D(not_8_out), .Q(PlDirCh), .clk(not_8_out), .clr(not_10_out));  // open: en
  not not_9 (not_9_out, not_8_out);
  not not_10 (not_10_out, not_9_out);
  Subtractor subtractor_2 (.a(PLyOM), .b(8'h1), .out(subtractor_2_out));  // open: bin, bout
  assign NewPLyOM = and_1_out ? subtractor_2_out : 8'bz;  // Controlled_Buffer controlled_buffer_1
  Adder adder_2 (.a(PLyOM), .b(8'h1), .out(adder_2_out));  // open: cin, cout
  assign NewPLyOM = and_2_out ? adder_2_out : 8'bz;  // Controlled_Buffer controlled_buffer_2
  assign NewPLxOM = and_3_out ? adder_3_out : 8'bz;  // Controlled_Buffer controlled_buffer_3
  Adder adder_3 (.a(PLxOM), .b(8'h1), .out(adder_3_out));  // open: cin, cout
  assign NewPLxOM = and_4_out ? subtractor_3_out : 8'bz;  // Controlled_Buffer controlled_buffer_4
  Subtractor subtractor_3 (.a(PLxOM), .b(8'h1), .out(subtractor_3_out));  // open: bin, bout
  Register #(.width(4)) register_5 (.D(gSto), .Q(gameState), .clk(StateCh), .clr(mainRES));  // open: en
  Multiplexer #(.width(2)) multiplexer_3 (
    .in0(adder_1_out), .in1(subtractor_1_out), .out(NewPlDir), .sel(comparator_10_eq));  // open: en
  Comparator #(.width(4)) comparator_12 (.a(4'b0000), .b(gameState), .eq(gS0));  // open: gt, lt
  Comparator #(.width(4)) comparator_13 (.a(4'b0001), .b(gameState), .eq(gS1));  // open: gt, lt
  Comparator #(.width(4)) comparator_14 (.a(4'b0010), .b(gameState), .eq(gS2));  // open: gt, lt
  Register #(.width(2)) register_6 (.D(NewPlDir), .Q(PlDir), .clk(PlDirCh), .clr(mainRES));  // open: en
  or or_6 (InpFl, InpFlmove2, InpFlmove1);
  or or_7 (or_7_out, and_1_out, and_2_out);
  Register #(.width(1)) register_7 (.D(or_7_out), .Q(changePCy), .clk(or_7_out), .clr(not_12_out));  // open: en
  not not_11 (not_11_out, or_7_out);
  not not_12 (not_12_out, not_11_out);
  or or_8 (InpFlmove2, or_7_out, or_9_out);
  Register #(.width(1)) register_8 (.D(or_9_out), .Q(changePCx), .clk(or_9_out), .clr(not_13_out));  // open: en
  or or_9 (or_9_out, and_3_out, and_4_out);
  not not_13 (not_13_out, not_14_out);
  not not_14 (not_14_out, or_9_out);
  Register #(.width(1)) register_9 (.D(and_5_out), .Q(register_9_q), .clk(and_5_out), .clr(not_15_out));  // open: en
  and and_5 (and_5_out, InpFlpre, gS0);
  not not_15 (not_15_out, not_16_out);
  not not_16 (not_16_out, and_5_out);
  buf buffer_1 (LoadMap, and_5_out);
  Register #(.width(1)) register_10 (.D(chGM), .Q(register_10_q), .clk(chGM), .clr(not_18_out));  // open: en
  not not_17 (not_17_out, chGM);
  not not_18 (not_18_out, not_17_out);
  buf buffer_2 (out_1, InpFl);
  Subtractor subtractor_4 (.a(PLyOM), .b(8'h1), .out(subtractor_4_out));  // open: bin, bout
  Adder adder_4 (.a(PLyOM), .b(8'h1), .out(adder_4_out));  // open: cin, cout
  Subtractor subtractor_5 (.a(PLxOM), .b(8'h1), .out(subtractor_5_out));  // open: bin, bout
  Adder adder_5 (.a(PLxOM), .b(8'h1), .out(adder_5_out));  // open: cin, cout
  or or_10 (StateCh, register_9_q, register_10_q);
  Multiplexer #(.select(2), .width(4)) multiplexer_4 (
    .in0(4'b0001), .in1(4'b0010), .in2(4'b0001), .out(gSto), .sel({gS2, gS1}));  // open: in3, en
  Multiplexer #(.select(2), .width(8)) multiplexer_5 (
    .in0(8'h1f), .in1({8{1'b0}}), .in2(8'h1e), .out(gStdtScrMem), .sel({gS2, gS1}));  // open: in3, en
  graphic_elems graphic_elems_1 (.ADDR(gStdtScrMem), .ELEM(memN), .DATA(memChar), .LEN(tpLen));
  Button button_2 (.out(memReadyToPrint));
  x_y__to_memory_elem_number x_y_____elem (.H(MapW), .Y(PLyOM), .X(PLxOM), .ELEM(x_y_____elem_elem), .START(12'h4));
  x_y__to_memory_elem_number x_y_____elem_2 (
    .H(MapW), .Y(subtractor_4_out), .X(PLxOM), .ELEM(x_y_____elem_2_elem), .START(12'h4));
  x_y__to_memory_elem_number x_y_____elem_3 (
    .H(MapW), .Y(adder_4_out), .X(PLxOM), .ELEM(x_y_____elem_3_elem), .START(12'h4));
  x_y__to_memory_elem_number x_y_____elem_4 (
    .H(MapW), .Y(PLyOM), .X(subtractor_5_out), .ELEM(x_y_____elem_4_elem), .START(12'h4));
  x_y__to_memory_elem_number x_y_____elem_5 (
    .H(MapW), .Y(PLyOM), .X(adder_5_out), .ELEM(x_y_____elem_5_elem), .START(12'h4));
  Button button_3 (.out(chGM));
  maps maps_2 (.ADDR(mapLevelCur), .ELEM(x_y_____elem_elem), .DATA(p_x_y));  // open: LEN, Xpp, Ypp, Width, Height
  maps maps_3 (.ADDR(mapLevelCur), .ELEM(x_y_____elem_2_elem), .DATA(p_x_y_1_t));  // open: LEN, Xpp, Ypp, Width, Height
  maps maps_4 (.ADDR(mapLevelCur), .ELEM(x_y_____elem_3_elem), .DATA(p_x_y_1));  // open: LEN, Xpp, Ypp, Width, Height
  maps maps_5 (.ADDR(mapLevelCur), .ELEM(x_y_____elem_4_elem), .DATA(p_x_1_y_t));  // open: LEN, Xpp, Ypp, Width, Height
  maps maps_6 (.ADDR(mapLevelCur), .ELEM(x_y_____elem_5_elem), .DATA(p_x_1_y));  // open: LEN, Xpp, Ypp, Width, Height

  // Notes on the sheet:
  //   MOVE PART
  //   inp: w
  //   START
  //   inp: a
  //   inp: d
  //   Curent map level
  //   Curent text toprint
  //   Game state
  //   0 - start screen 1 - walking 2 - atack
  //   0
  //   ->
  //   3
  //   1
  //   2
  //   Player Direction
  //   1 
  //   1 если прочитан вход
  //   символ входа
  //   Player (y-1,x) cell
  //   Player (y+1,x) cell
  //   Player (y,x-1) cell
  //   Player (y,x+1) cell
  //   Change game mode(... - walkeng - atack - ...)
  //   Player cell
  //   Player cell
endmodule

// CP
module consoler (
  input  CLK,
  input  [7:0] MEM_D,
  input  [11:0] PRINT_SIZE,
  input  RESET,
  output IT_WORKED,
  output [7:0] INPUT_CHAR,
  output [11:0] MEM_A
);

  wire adder_1_out, and_3_out, and_4_out, clc, comparator_2_eq, not_1_out, not_2_out, not_3_out, not_4_out,
       not_5_out, or_2_out, PRND, readConsole, register_1_q, register_2_q, RES, RESET_MEMORY_COUNTER_out,
       uart_1_p3, uart_1_p6, uart_1_p8;
  wire [7:0] uart_1_p1;
  wire [11:0] adder_2_out;

  not not_1 (not_1_out, RESET);
  Register #(.width(1)) register_1 (.D(RESET), .Q(register_1_q), .clk(RESET), .clr(not_2_out));  // open: en
  not not_2 (not_2_out, not_1_out);
  and and_1 (clc, CLK, not_3_out);
  not not_3 (not_3_out, RES);
  or or_1 (RES, register_1_q, RESET_MEMORY_COUNTER_out);
  Button RESET_MEMORY_COUNTER (.out(RESET_MEMORY_COUNTER_out));
  and and_2 (IT_WORKED, not_5_out, PRND, register_2_q);
  Register #(.width(1)) register_2 (.D(adder_1_out), .Q(register_2_q), .clk(or_2_out));  // open: en, clr
  or or_2 (or_2_out, RES, uart_1_p3);
  not not_4 (not_4_out, PRND);
  not not_5 (not_5_out, uart_1_p3);
  Adder #(.width(1)) adder_1 (.a(register_2_q), .b(1'b1), .out(adder_1_out));  // open: cin, cout
  Register #(.width(12)) register_3 (.D(adder_2_out), .Q(MEM_A), .clk(and_3_out), .clr(RES));  // open: en
  not not_6 (readConsole, PRND);
  and and_3 (and_3_out, not_4_out, clc);
  Adder #(.width(12)) adder_2 (.a(MEM_A), .b(12'h1), .out(adder_2_out));  // open: cin, cout
  Register register_4 (.D(uart_1_p1), .Q(INPUT_CHAR), .clk(and_4_out), .clr(RES));  // open: en
  and and_4 (and_4_out, clc, comparator_2_eq);
  Comparator #(.width(12)) comparator_1 (.a(MEM_A), .b(PRINT_SIZE), .eq(PRND));  // open: gt, lt
  Comparator comparator_2 (.a(INPUT_CHAR), .b({8{1'b0}}), .eq(comparator_2_eq));  // open: gt, lt
  // UART uart_1: pin names not known; wires that end beside it: uart_1_p1, MEM_D, uart_1_p3, clc, uart_1_p3, uart_1_p6, uart_1_p6, uart_1_p8
  or or_3 (uart_1_p8, uart_1_p3, readConsole);

  // Notes on the sheet:
  //   Frame Printed
  //   Print Frame
  //   Input writened
  //   12 бит адрес
endmodule

// GE
module graphic_elems (
  input  [7:0] ADDR,
  input  [11:0] ELEM,
  output [7:0] DATA,
  output [11:0] LEN
);

  wire [7:0] deMux1, geD0, geD1, geD2, geD2_0, geD2_1, geD3, geD4, geD5, geD6, geD7, geD8, geD9, geD10,
       geD11, geD12, geD13, geD14, geD15;
  wire [11:0] deMuxl1;

  ROM #(.addrWidth(12)) rom_1 (.addr(ELEM), .data(geD0));  // open: sel
  ROM #(.addrWidth(12)) rom_2 (.addr(ELEM), .data(geD1));  // open: sel
  ROM #(.addrWidth(12)) rom_3 (.addr(ELEM), .data(geD2));  // open: sel
  ROM #(.addrWidth(12)) rom_4 (.addr(ELEM), .data(geD3));  // open: sel
  ROM #(.addrWidth(12)) rom_5 (.addr(ELEM), .data(geD4));  // open: sel
  ROM #(.addrWidth(12)) rom_6 (.addr(ELEM), .data(geD5));  // open: sel
  ROM #(.addrWidth(12)) rom_7 (.addr(ELEM), .data(geD6));  // open: sel
  ROM #(.addrWidth(12)) rom_8 (.addr(ELEM), .data(geD7));  // open: sel
  ROM #(.addrWidth(12)) rom_9 (.addr(ELEM), .data(geD8));  // open: sel
  ROM #(.addrWidth(12)) rom_10 (.addr(ELEM), .data(geD9));  // open: sel
  ROM #(.addrWidth(12)) rom_11 (.addr(ELEM), .data(geD10));  // open: sel
  ROM #(.addrWidth(12)) rom_12 (.addr(ELEM), .data(geD11));  // open: sel
  ROM #(.addrWidth(12)) rom_13 (.addr(ELEM), .data(geD12));  // open: sel
  ROM #(.addrWidth(12)) rom_14 (.addr(ELEM), .data(geD13));  // open: sel
  ROM #(.addrWidth(12)) rom_15 (.addr(ELEM), .data(geD14));  // open: sel
  ROM #(.addrWidth(12)) rom_16 (.addr(ELEM), .data(geD15));  // open: sel
  ROM #(.addrWidth(12)) rom_17 (.addr(ELEM), .data(geD2_0));  // open: sel
  ROM #(.addrWidth(12)) rom_18 (.addr(ELEM), .data(geD2_1));  // open: sel
  Multiplexer #(.select(5), .width(8)) multiplexer_1 (
    .in0(geD0), .in1(geD1), .in2(geD2), .in3(geD3), .in4(geD4), .in5(geD5), .in6(geD6), .in7(geD7),
    .in8(geD8), .in9(geD9), .in10(geD10), .in11(geD11), .in12(geD12), .in13(geD13), .in14(geD14),
    .in15(geD15), .in30(geD2_1), .in31(geD2_0), .out(deMux1), .sel(ADDR[4:0]));  // open: in16, in17, in18, in19, in20, in21, in22, in23, in24, in25, in26, in27, in28, in29, en
  Multiplexer #(.select(5), .width(12)) multiplexer_2 (
    .in0(12'had5), .in1(12'h596), .in2(12'h596), .in3(12'h596), .in4(12'h596), .in5(12'h596), .in6(12'h596),
    .in7(12'h596), .in8(12'h596), .in9(12'h596), .in10(12'h596), .in11(12'h596), .in12(12'h596),
    .in13(12'h596), .in14(12'h596), .in15(12'h596), .in30(12'had5), .in31(12'had5), .out(deMuxl1),
    .sel(ADDR[4:0]));  // open: in16, in17, in18, in19, in20, in21, in22, in23, in24, in25, in26, in27, in28, in29, en
  Multiplexer #(.select(3), .width(8)) multiplexer_3 (
    .in0(deMux1), .out(DATA), .sel(ADDR[7:5]));  // open: in1, in2, in3, in4, in5, in6, in7, en
  Multiplexer #(.select(3), .width(12)) multiplexer_4 (
    .in0(deMuxl1), .out(LEN), .sel(ADDR[7:5]));  // open: in1, in2, in3, in4, in5, in6, in7, en

  // Other names for the same wires on the sheet: geAddr1[4:0] = ADDR[4:0]; geAddr2[2:0] = ADDR[7:5];
  //   geEl[11:0] = ELEM

  // Notes on the sheet:
  //   BOARD
  //   contents of rom_1 (hex, n*v repeats v):
  //   0 76*23 a 23 52*20 23 21*20 23 a 23 52*20 23 21*20 23 a 23 52*20 23 21*20 23 a 23 52*20 23 21*20 23
  //   a 23 52*20 23 21*20 23 a 23 52*20 23 21*20 23 a 23 52*20 23 21*20 23 a 23 52*20 23 21*20 23 a 23
  //   52*20 23 21*20 23 a 23 52*20 23 21*20 23 a 23 52*20 23 21*20 23 a 23 52*20 23 21*20 23 a 23 52*20 23
  //   21*20 23 a 23 52*20 23 21*20 23 a 23 52*20 23 21*20 23 a 23 52*20 23 21*20 23 a 23 52*20 23 21*20 23
  //   a 23 52*20 23 21*20 23 a 23 52*20 23 21*20 23 a 23 52*20 23 21*20 23 a 23 52*20 23 21*20 23 a 23
  //   52*20 23*23 a 23 52*20 23 21*20 23 a 23 52*20 23 21*20 23 a 23 52*20 23 21*20 23 a 23 52*20 23 21*20
  //   23 a 23 52*20 23 21*20 23 a 76*23 a 23 74*20 23 a 76*23 a 23 9*20 23 9*20 23 9*20 23 9*20 23 9*20 23
  //   20 48 50 20 7c 10*20 7c 28 20 20 2f 31 30 29 20 23 a 23 9*20 23 9*20 23 9*20 23 9*20 23 9*20 23 20
  //   53 54 20 7c 10*20 7c 28 20 20 2f 31 30 29 20 23 a 23 9*20 23 9*20 23 9*20 23 9*20 23 9*20 23 20 48
  //   47 20 7c 10*20 7c 28 20 20 2f 31 30 29 20 23 a 23 9*20 23 9*20 23 9*20 23 9*20 23 9*20 23 24*20 23 a
  //   76*23 a 52*20
  //   FFL
  //   contents of rom_2 (hex, n*v repeats v):
  //   0 51*20 a 52*20 a 52*20 a 9*20 34*5f 9*20 a 8*20 7c 34*23 7c 8*20 a 8*20 7c 34*23 7c 8*20 a 8*20 7c
  //   34*23 7c 8*20 a 8*20 7c 34*23 7c 8*20 a 8*20 7c 34*23 7c 8*20 a 8*20 7c 34*23 7c 8*20 a 8*20 7c
  //   34*23 7c 8*20 a 8*20 7c 34*23 7c 8*20 a 8*20 7c 34*23 7c 8*20 a 8*20 7c 34*23 7c 8*20 a 8*20 7c
  //   34*23 7c 8*20 a 8*20 7c 34*23 7c 8*20 a 8*20 7c 34*23 7c 8*20 a 8*20 7c 34*23 7c 8*20 a 8*20 7c
  //   34*23 7c 8*20 a 8*20 7c 34*23 7c 8*20 a 8*20 7c 34*23 7c 8*20 a 8*20 7c 34*23 7c 8*20 a 8*20 7c
  //   34*23 7c 8*20 a 52*20 a 52*20 a 52*20 a 52*20
  //   FFFL
  //   contents of rom_3 (hex, n*v repeats v):
  //   0 51*20 a 52*20 a 52*20 a 52*20 a 52*20 a 52*20 a 52*20 a 18*20 16*5f 18*20 a 17*20 7c 16*23 7c
  //   17*20 a 17*20 7c 16*23 7c 17*20 a 17*20 7c 16*23 7c 17*20 a 17*20 7c 16*23 7c 17*20 a 17*20 7c 16*23
  //   7c 17*20 a 17*20 7c 16*23 7c 17*20 a 17*20 7c 16*23 7c 17*20 a 17*20 7c 16*23 7c 17*20 a 17*20 7c
  //   16*23 7c 17*20 a 17*20 7c 16*23 7c 17*20 a 17*20 7c 16*23 7c 17*20 a 52*20 a 52*20 a 52*20 a 52*20 a
  //   52*20 a 52*20 a 52*20 a 52*20
  //   FFFFL
  //   contents of rom_4 (hex, n*v repeats v):
  //   0 51*20 a 52*20 a 52*20 a 52*20 a 52*20 a 52*20 a 52*20 a 52*20 a 52*20 a 52*20 a 24*20 4*5f 24*20 a
  //   23*20 7c 4*23 7c 23*20 a 23*20 7c 4*23 7c 23*20 a 23*20 7c 4*23 7c 23*20 a 23*20 7c 4*23 7c 23*20 a
  //   23*20 7c 4*23 7c 23*20 a 52*20 a 52*20 a 52*20 a 52*20 a 52*20 a 52*20 a 52*20 a 52*20 a 52*20 a
  //   52*20 a 52*20
  //   LFL
  //   contents of rom_5 (hex, n*v repeats v):
  //   0 5c 5f 49*20 a 23 23 5c 5f 48*20 a 4*23 5c 5f 46*20 a 6*23 5c 5f 44*20 a 8*23 7c 43*20 a 8*23 7c
  //   43*20 a 8*23 7c 43*20 a 8*23 7c 43*20 a 8*23 7c 43*20 a 8*23 7c 43*20 a 8*23 7c 43*20 a 8*23 7c
  //   43*20 a 8*23 7c 43*20 a 8*23 7c 43*20 a 8*23 7c 43*20 a 8*23 7c 43*20 a 8*23 7c 43*20 a 8*23 7c
  //   43*20 a 8*23 7c 43*20 a 8*23 7c 43*20 a 8*23 7c 43*20 a 8*23 7c 43*20 a 8*23 7c 43*20 a 6*23 2f
  //   45*20 a 4*23 2f 47*20 a 23 23 2f 49*20 a 2f 51*20
  //   LFFL
  //   contents of rom_6 (hex, n*v repeats v):
  //   0 51*20 a 52*20 a 52*20 a 8*5f 44*20 a 8*23 7c 43*20 a 8*23 7c 43*20 a 8*23 7c 43*20 a 8*23 7c 43*20
  //   a 8*23 7c 43*20 a 8*23 7c 43*20 a 8*23 7c 43*20 a 8*23 7c 43*20 a 8*23 7c 43*20 a 8*23 7c 43*20 a
  //   8*23 7c 43*20 a 8*23 7c 43*20 a 8*23 7c 43*20 a 8*23 7c 43*20 a 8*23 7c 43*20 a 8*23 7c 43*20 a 8*23
  //   7c 43*20 a 8*23 7c 43*20 a 8*23 7c 43*20 a 52*20 a 52*20 a 52*20 a 52*20
  //   LFFFL
  //   contents of rom_7 (hex, n*v repeats v):
  //   0 51*20 a 52*20 a 52*20 a 52*20 a 52*20 a 52*20 a 52*20 a 17*5f 35*20 a 17*23 7c 34*20 a 17*23 7c
  //   34*20 a 17*23 7c 34*20 a 17*23 7c 34*20 a 17*23 7c 34*20 a 17*23 7c 34*20 a 17*23 7c 34*20 a 17*23
  //   7c 34*20 a 17*23 7c 34*20 a 17*23 7c 34*20 a 17*23 7c 34*20 a 52*20 a 52*20 a 52*20 a 52*20 a 52*20
  //   a 52*20 a 52*20 a 52*20
  //   LFFFFL
  //   contents of rom_8 (hex, n*v repeats v):
  //   0 51*20 a 52*20 a 52*20 a 52*20 a 52*20 a 52*20 a 52*20 a 52*20 a 52*20 a 52*20 a 18*20 5*5f 29*20 a
  //   17*20 7c 5*23 7c 28*20 a 17*20 7c 5*23 7c 28*20 a 17*20 7c 5*23 7c 28*20 a 17*20 7c 5*23 7c 28*20 a
  //   17*20 7c 5*23 7c 28*20 a 52*20 a 52*20 a 52*20 a 52*20 a 52*20 a 52*20 a 52*20 a 52*20 a 52*20 a
  //   52*20 a 52*20
  //   RFL
  //   contents of rom_9 (hex, n*v repeats v):
  //   0 50*20 5f 2f a 48*20 5f 2f 23 23 a 46*20 5f 2f 4*23 a 44*20 5f 2f 6*23 a 43*20 7c 8*23 a 43*20 7c
  //   8*23 a 43*20 7c 8*23 a 43*20 7c 8*23 a 43*20 7c 8*23 a 43*20 7c 8*23 a 43*20 7c 8*23 a 43*20 7c 8*23
  //   a 43*20 7c 8*23 a 43*20 7c 8*23 a 43*20 7c 8*23 a 43*20 7c 8*23 a 43*20 7c 8*23 a 43*20 7c 8*23 a
  //   43*20 7c 8*23 a 43*20 7c 8*23 a 43*20 7c 8*23 a 43*20 7c 8*23 a 43*20 7c 8*23 a 45*20 5c 6*23 a
  //   47*20 5c 4*23 a 49*20 5c 23 23 a 51*20 5c
  //   RFFL
  //   contents of rom_10 (hex, n*v repeats v):
  //   0 51*20 a 52*20 a 52*20 a 52*20 a 41*20 5f 2f 7c 8*20 a 39*20 5f 2f 23 23 7c 8*20 a 37*20 5f 2f 4*23
  //   7c 8*20 a 35*20 5f 2f 6*23 7c 8*20 a 34*20 7c 8*23 7c 8*20 a 34*20 7c 8*23 7c 8*20 a 34*20 7c 8*23
  //   7c 8*20 a 34*20 7c 8*23 7c 8*20 a 34*20 7c 8*23 7c 8*20 a 34*20 7c 8*23 7c 8*20 a 34*20 7c 8*23 7c
  //   8*20 a 34*20 7c 8*23 7c 8*20 a 34*20 7c 8*23 7c 8*20 a 34*20 7c 8*23 7c 8*20 a 34*20 7c 8*23 7c 8*20
  //   a 36*20 5c 6*23 7c 8*20 a 38*20 5c 4*23 7c 8*20 a 40*20 5c 23 23 7c 8*20 a 42*20 5c 7c 8*20 a 52*20
  //   a 52*20 a 52*20 a 52*20
  //   RFFFL
  //   contents of rom_11 (hex, n*v repeats v):
  //   0 51*20 a 52*20 a 52*20 a 52*20 a 52*20 a 52*20 a 52*20 a 35*20 17*5f a 34*20 7c 17*23 a 34*20 7c
  //   17*23 a 34*20 7c 17*23 a 34*20 7c 17*23 a 34*20 7c 17*23 a 34*20 7c 17*23 a 34*20 7c 17*23 a 34*20
  //   7c 17*23 a 34*20 7c 17*23 a 34*20 7c 17*23 a 34*20 7c 17*23 a 52*20 a 52*20 a 52*20 a 52*20 a 52*20
  //   a 52*20 a 52*20 a 52*20
  //   RFFFFL
  //   contents of rom_12 (hex, n*v repeats v):
  //   0 51*20 a 52*20 a 52*20 a 52*20 a 52*20 a 52*20 a 52*20 a 52*20 a 52*20 a 52*20 a 29*20 5*5f 18*20 a
  //   28*20 7c 5*23 7c 17*20 a 28*20 7c 5*23 7c 17*20 a 28*20 7c 5*23 7c 17*20 a 28*20 7c 5*23 7c 17*20 a
  //   28*20 7c 5*23 7c 17*20 a 52*20 a 52*20 a 52*20 a 52*20 a 52*20 a 52*20 a 52*20 a 52*20 a 52*20 a
  //   52*20 a 52*20
  //   FRFL
  //   contents of rom_13 (hex, n*v repeats v):
  //   0 51*20 a 52*20 a 52*20 a 52*20 a 41*20 5f 2f 7c 8*20 a 39*20 5f 2f 23 23 7c 8*20 a 37*20 5f 2f 4*23
  //   7c 8*20 a 35*20 5f 2f 6*23 7c 8*20 a 34*20 7c 8*23 7c 8*20 a 34*20 7c 8*23 7c 8*20 a 34*20 7c 8*23
  //   7c 8*20 a 34*20 7c 8*23 7c 8*20 a 34*20 7c 8*23 7c 8*20 a 34*20 7c 8*23 7c 8*20 a 34*20 7c 8*23 7c
  //   8*20 a 34*20 7c 8*23 7c 8*20 a 34*20 7c 8*23 7c 8*20 a 34*20 7c 8*23 7c 8*20 a 34*20 7c 8*23 7c 8*20
  //   a 36*20 5c 6*23 7c 8*20 a 38*20 5c 4*23 7c 8*20 a 40*20 5c 23 23 7c 8*20 a 42*20 5c 7c 8*20 a 52*20
  //   a 52*20 a 52*20 a 52*20
  //   FLFL
  //   contents of rom_14 (hex, n*v repeats v):
  //   0 51*20 a 52*20 a 52*20 a 52*20 a 8*20 7c 5c 5f 41*20 a 8*20 7c 23 23 5c 5f 39*20 a 8*20 7c 4*23 5c
  //   5f 37*20 a 8*20 7c 6*23 5c 5f 35*20 a 8*20 7c 8*23 7c 34*20 a 8*20 7c 8*23 7c 34*20 a 8*20 7c 8*23
  //   7c 34*20 a 8*20 7c 8*23 7c 34*20 a 8*20 7c 8*23 7c 34*20 a 8*20 7c 8*23 7c 34*20 a 8*20 7c 8*23 7c
  //   34*20 a 8*20 7c 8*23 7c 34*20 a 8*20 7c 8*23 7c 34*20 a 8*20 7c 8*23 7c 34*20 a 8*20 7c 8*23 7c
  //   34*20 a 8*20 7c 6*23 2f 36*20 a 8*20 7c 4*23 2f 38*20 a 8*20 7c 23 23 2f 40*20 a 8*20 7c 2f 42*20 a
  //   52*20 a 52*20 a 52*20 a 52*20
  //   FFRFL
  //   contents of rom_15 (hex, n*v repeats v):
  //   0 51*20 a 52*20 a 52*20 a 52*20 a 52*20 a 52*20 a 52*20 a 52*20 a 32*20 5f 2f 7c 17*20 a 30*20 5f 2f
  //   23 23 7c 17*20 a 29*20 2f 4*23 7c 17*20 a 28*20 7c 5*23 7c 17*20 a 28*20 7c 5*23 7c 17*20 a 28*20 7c
  //   5*23 7c 17*20 a 28*20 7c 5*23 7c 17*20 a 28*20 7c 5*23 7c 17*20 a 29*20 5c 4*23 7c 17*20 a 31*20 5c
  //   23 23 7c 17*20 a 33*20 5c 7c 17*20 a 52*20 a 52*20 a 52*20 a 52*20 a 52*20 a 52*20 a 52*20 a 52*20
  //   FFLFL
  //   contents of rom_16 (hex, n*v repeats v):
  //   0 51*20 a 52*20 a 52*20 a 52*20 a 52*20 a 52*20 a 52*20 a 52*20 a 17*20 7c 5c 5f 32*20 a 17*20 7c 23
  //   23 5c 5f 30*20 a 17*20 7c 4*23 5c 29*20 a 17*20 7c 5*23 7c 28*20 a 17*20 7c 5*23 7c 28*20 a 17*20 7c
  //   5*23 7c 28*20 a 17*20 7c 5*23 7c 28*20 a 17*20 7c 5*23 7c 28*20 a 17*20 7c 4*23 2f 29*20 a 17*20 7c
  //   23 23 2f 31*20 a 17*20 7c 2f 33*20 a 52*20 a 52*20 a 52*20 a 52*20 a 52*20 a 52*20 a 52*20 a 52*20
  //   contents of rom_17 (hex, n*v repeats v):
  //   0 76*23 a 23 74*20 23 a 23 74*20 23 a 23 74*20 23 a 23 26*20 5*5f 20 20 5f 40*20 23 a 23 25*20 7c 5f
  //   20 20 20 5f 7c 7c 20 7c 39*20 23 a 23 27*20 7c 20 7c 20 20 7c 20 7c 5f 5f 4*20 5f 5f 5f 30*20 23 a
  //   23 27*20 7c 20 7c 20 20 7c 20 27 5f 20 5c 20 20 2f 20 5f 20 5c 29*20 23 a 23 27*20 7c 20 7c 20 20 7c
  //   20 7c 20 7c 20 7c 7c 20 20 5f 5f 2f 29*20 23 a 23 27*20 5c 5f 2f 20 20 7c 5f 7c 20 7c 5f 7c 20 5c 5f
  //   5f 5f 7c 29*20 23 a 23 20 5f 5f 5f 20 20 5f 5f 5f 8*20 5f 7*20 5f 7*20 5f 40*20 23 a 23 20 7c 20 20
  //   5c 2f 20 20 7c 7*20 7c 20 7c 5*20 28 20 29 5*20 7c 20 7c 39*20 23 a 23 20 7c 20 2e 20 20 2e 20 7c 20
  //   20 5f 5f 5f 20 20 7c 20 7c 20 20 5f 5f 5f 7c 2f 20 5f 5f 5f 20 20 7c 20 7c 5f 5f 20 20 20 5f 20 20
  //   20 5f 20 20 5f 20 5f 5f 20 20 5f 20 5f 5f 20 20 5f 5f 5f 20 5f 5f 6*20 5f 5f 20 23 a 23 20 7c 20 7c
  //   5c 2f 7c 20 7c 20 2f 20 5f 20 5c 20 7c 20 7c 20 2f 20 5f 20 5c 20 2f 20 5f 5f 7c 20 7c 20 27 5f 20
  //   5c 20 7c 20 7c 20 7c 20 7c 7c 20 27 5f 5f 7c 7c 20 27 5f 5f 7c 2f 20 5f 20 5c 5c 20 5c 20 2f 5c 20
  //   2f 20 2f 20 23 a 23 20 7c 20 7c 20 20 7c 20 7c 7c 20 28 5f 29 20 7c 7c 20 7c 7c 20 20 5f 5f 2f 20 5c
  //   5f 5f 20 5c 20 7c 20 7c 5f 29 20 7c 7c 20 7c 5f 7c 20 7c 7c 20 7c 20 20 20 7c 20 7c 20 20 7c 20 28
  //   5f 29 20 7c 5c 20 56 20 20 56 20 2f 20 20 23 a 23 20 5c 5f 7c 20 20 7c 5f 2f 20 5c 5f 5f 5f 2f 20 7c
  //   5f 7c 20 5c 5f 5f 5f 7c 20 7c 5f 5f 5f 2f 20 7c 5f 2e 5f 5f 2f 20 20 5c 5f 5f 2c 5f 7c 7c 5f 7c 20
  //   20 20 7c 5f 7c 20 20 20 5c 5f 5f 5f 2f 20 20 5c 5f 2f 5c 5f 2f 20 20 20 23 a 23 74*20 23 a 23 74*20
  //   23 a 23 74*20 23 a 23 74*20 23 a 23 74*20 23 a 23 74*20 23 a 23 74*20 23 a 23 74*20 23 a 23 74*20 23
  //   a 23 74*20 23 a 23 74*20 23 a 23 74*20 23 a 23 74*20 23 a 23 74*20 23 a 23 74*20 23 a 23 74*20 23 a
  //   23 74*20 23 a 23 39*20 50 52 45 53 53 20 41 4e 59 20 4b 45 59 20 54 4f 20 43 4f 4e 54 49 4e 55 45 2e
  //   2e 2e 7*20 23 a 23 74*20 23 a 76*23 a 52*20
  //   contents of rom_18 (hex, n*v repeats v):
  //   0 76*23 a 23 74*20 23 a 23 74*20 23 a 23 74*20 23 a 23 74*20 23 a 23 74*20 23 a 23 74*20 23 a 23
  //   74*20 23 a 23 74*20 23 a 23 9*20 7c 14*20 7c 13*20 7c 24*20 7c 20 28 20 20 7c 20 20 29 20 20 23 a 23
  //   74*20 23 a 23 74*20 23 a 23 74*20 23 a 23 74*20 23 a 23 74*20 23 a 23 74*20 23 a 23 74*20 23 a 23
  //   74*20 23 a 23 74*20 23 a 23 4*20 65*2d 5*20 23 a 23 74*20 23 a 23 20*20 5e 24*20 2e 28*20 23 a 23
  //   8*20 2e 19*20 2e 10*20 2e 18*20 2e 7*20 2e 7*20 23 a 23 16*20 2e 17*20 2e 17*20 5e 7*20 2e 13*20 23
  //   a 23 23*20 2e 18*20 2e 31*20 23 a 23 6*20 2e 6*20 5e 16*20 5e 23*20 2e 19*20 23 a 23 23*20 2e 11*20
  //   2e 5*20 2e 20*20 5e 11*20 23 a 23 74*20 23 a 76*23 a 23 74*20 23 a 76*23 a 23 9*20 23 9*20 23 9*20
  //   23 9*20 23 9*20 23 20 48 50 20 7c 10*20 7c 28 20 20 2f 31 30 29 20 23 a 23 9*20 23 9*20 23 9*20 23
  //   9*20 23 9*20 23 20 53 54 20 7c 10*20 7c 28 20 20 2f 31 30 29 20 23 a 23 9*20 23 9*20 23 9*20 23 9*20
  //   23 9*20 23 20 48 47 20 7c 10*20 7c 28 20 20 2f 31 30 29 20 23 a 23 9*20 23 9*20 23 9*20 23 9*20 23
  //   9*20 23 24*20 23 a 76*23 a 52*20
  //   START SCREEN
  //   ATACK BOARD
endmodule

// Maps
module maps (
  input  [7:0] ADDR,
  input  [11:0] ELEM,
  output [11:0] Width,
  output [11:0] Height,
  output [7:0] Xpp,
  output [7:0] Ypp,
  output [7:0] DATA,
  output [11:0] LEN
);

  wire [7:0] mgeD0, undriven_4, undriven_5;
  wire [11:0] undriven, undriven_2, undriven_3;

  ROM #(.addrWidth(12)) rom_1 (.addr(ELEM), .data(mgeD0));  // open: sel
  Multiplexer #(.select(5), .width(8)) multiplexer_1 (
    .in0(mgeD0), .out(DATA), .sel(ADDR[4:0]));  // open: in1, in2, in3, in4, in5, in6, in7, in8, in9, in10, in11, in12, in13, in14, in15, in16, in17, in18, in19, in20, in21, in22, in23, in24, in25, in26, in27, in28, in29, in30, in31, en
  Multiplexer #(.select(5), .width(12)) multiplexer_2 (
    .in0(12'h99), .in30(undriven), .in31(undriven), .out(LEN), .sel(ADDR[4:0]));  // open: in1, in2, in3, in4, in5, in6, in7, in8, in9, in10, in11, in12, in13, in14, in15, in16, in17, in18, in19, in20, in21, in22, in23, in24, in25, in26, in27, in28, in29, en
  Multiplexer #(.select(5), .width(12)) multiplexer_3 (
    .in0(12'hb), .in30(undriven_2), .in31(undriven_2), .out(Width), .sel(ADDR[4:0]));  // open: in1, in2, in3, in4, in5, in6, in7, in8, in9, in10, in11, in12, in13, in14, in15, in16, in17, in18, in19, in20, in21, in22, in23, in24, in25, in26, in27, in28, in29, en
  Multiplexer #(.select(5), .width(12)) multiplexer_4 (
    .in0(12'h8), .in30(undriven_3), .in31(undriven_3), .out(Height), .sel(ADDR[4:0]));  // open: in1, in2, in3, in4, in5, in6, in7, in8, in9, in10, in11, in12, in13, in14, in15, in16, in17, in18, in19, in20, in21, in22, in23, in24, in25, in26, in27, in28, in29, en
  Multiplexer #(.select(5), .width(8)) multiplexer_5 (
    .in0(8'h3), .in30(undriven_4), .in31(undriven_4), .out(Xpp), .sel(ADDR[4:0]));  // open: in1, in2, in3, in4, in5, in6, in7, in8, in9, in10, in11, in12, in13, in14, in15, in16, in17, in18, in19, in20, in21, in22, in23, in24, in25, in26, in27, in28, in29, en
  Multiplexer #(.select(5), .width(8)) multiplexer_6 (
    .in0(8'h3), .in30(undriven_5), .in31(undriven_5), .out(Ypp), .sel(ADDR[4:0]));  // open: in1, in2, in3, in4, in5, in6, in7, in8, in9, in10, in11, in12, in13, in14, in15, in16, in17, in18, in19, in20, in21, in22, in23, in24, in25, in26, in27, in28, in29, en

  // Other names for the same wires on the sheet: mdeMux1[7:0] = DATA; mdeMuxl1[11:0] = LEN; mgeAddr1[4:0] = ADDR[4:0];
  //   mgeEl[11:0] = ELEM; mhMuxl1[11:0] = Height; mwMuxl1[11:0] = Width; mXMuxl1[7:0] = Xpp; mYMuxl1[7:0] = Ypp

  // Notes on the sheet:
  //   TEST MAP
  //   contents of rom_1 (hex, n*v repeats v):
  //   0 4 3 2 36*23 5*20 6*23 20 23 23 20 20 6*23 20 20 23 23 20 36*23
endmodule

module printing_map (
  input  [7:0] Curr_char,
  input  [7:0] height_of_map,
  input  [7:0] length_of_map,
  input  in_4
);

  wire button_1_out, comparator_1_eq, comparator_2_eq, comparator_3_eq, comparator_3_lt;
  wire [7:0] adder_1_out, controlled_buffer_1_out, register_1_q, register_2_q;

  Adder adder_1 (.a(register_1_q), .b(8'h1), .out(adder_1_out));  // open: cin, cout
  Register register_1 (.D(adder_1_out), .Q(register_1_q), .clk(in_4), .clr(button_1_out));  // open: en
  Button button_1 (.out(button_1_out));
  Comparator comparator_1 (.a(8'h1), .b(register_1_q), .eq(comparator_1_eq));  // open: gt, lt
  Comparator comparator_2 (.a(8'h2), .b(register_1_q), .eq(comparator_2_eq));  // open: gt, lt
  Comparator comparator_3 (.a(8'h3), .b(register_1_q), .eq(comparator_3_eq), .lt(comparator_3_lt));  // open: gt
  Register y (.D(Curr_char), .en(comparator_1_eq), .clk(in_4));  // open: Q, clr
  Register x (.D(Curr_char), .en(comparator_2_eq), .clk(in_4));  // open: Q, clr
  Register Direction (.D(Curr_char), .en(comparator_3_eq), .clk(in_4));  // open: Q, clr
  Register register_2 (.D(controlled_buffer_1_out), .Q(register_2_q), .clk(in_4));  // open: en, clr
  assign controlled_buffer_1_out = comparator_3_lt ? Curr_char : 8'bz;  // Controlled_Buffer controlled_buffer_1

  // Other names for the same wires on the sheet: Clock = in_4; height[7:0] = height_of_map;
  //   length[7:0] = length_of_map
endmodule

module x_y__to_memory_elem_number (
  input  [11:0] H,
  input  [7:0] Y,
  input  [7:0] X,
  input  [11:0] START,
  output [11:0] ELEM
);

  wire [11:0] adder_1_out, bit_extender_1_out, bit_extender_2_out, multiplier_1_out;

  assign bit_extender_1_out = {{4{1'b0}}, Y};  // Bit_Extender bit_extender_1
  Multiplier #(.width(12)) multiplier_1 (.a(H), .b(bit_extender_1_out), .out(multiplier_1_out));  // open: cin, cout
  assign bit_extender_2_out = {{4{1'b0}}, X};  // Bit_Extender bit_extender_2
  Adder #(.width(12)) adder_1 (.a(multiplier_1_out), .b(bit_extender_2_out), .out(adder_1_out));  // open: cin, cout
  Adder #(.width(12)) adder_2 (.a(adder_1_out), .b(START), .out(ELEM));  // open: cin, cout
endmodule
